# Fritzing sketch wiring diagram (saved by Fritzing 0.9.3b)
breadboards: 1

parts:
  Part2 = SparkFun VR IMU Breakout - BNO086 (Qwiic) [part_number=SEN-22857]
  SERVO1 = Tower Pro SG90 servo [part_number=101246]
  SERVO2 = Tower Pro SG90 servo [part_number=101246]
  SERVO3 = Tower Pro SG90 servo [part_number=101246]
  M1 = DC Motor
  Part3 = Adafruit DRV8871 [part_number="Adafruit #3190"]
  U5 = ESP32S-HiLetgo [part_number=ESP32S-HiLetgo]
  Mod1 = Raspberry Pi 4B
  J2 = XL4015 DC-DC CC CV module (blue)
  J3 = XL4015 DC-DC CC CV module (blue)
  Part5 = LIPO-2200mAh
  Part6 = LIPO-2200mAh
  Part7 = Adafruit PCA9685 PWM/Servo Breakout [part_number=815]
  Part4 = Rechargable Power Bank Battery Pack USB-A (2x Out) USB-C (In/Out)
  F2 = Fan - Ventilador [package=THT]
  J1 = Basic Servo
  URM47V1 = URM47V32
  URM47V2 = URM47V32
  URM47V3 = URM47V32
  URM47V4 = URM47V32

nets:
  GND: Part2.GND, U5.GND
  +5V: Part2.3.3V, J3.pin_3, URM47V1.+5V, URM47V2.+5V, URM47V3.+5V, URM47V4.+5V
  N1: Part2.SCL/SCK/RX, U5.GPIO22, U5.GPIO23
  N2: Part2.SDA/MISO/TX, U5.GPIO21, U5.GPIO3
  N3: SERVO1.Signal, Part7.PWM12
  +5V_2: SERVO1.+5V, SERVO2.+5V, SERVO3.+5V, Part7.5.0V, F2.5V, J1.vcc
  GND_2: SERVO1.GND, SERVO2.GND, SERVO3.GND, J2.pin_2, J3.pin_2, Part5.-, Part7.GND, F2.GND, J1.gnd
  N4: SERVO2.Signal, Part7.PWM8
  N5: SERVO3.Signal, Part7.PWM15
  N6: M1.pin_1, Part3.VMOTOR
  N7: M1.pin_2, Part3.GND
  N8: Part3.OUT2, J2.pin_4
  N9: Part3.OUT1, J2.pin_3
  N10: U5.pin_40, Mod1.USB
  N11: Mod1.GPIO17, URM47V1.COMP/TRIG
  N12: Mod1.GPIO27, URM47V2.COMP/TRIG
  N13: Mod1.GPIO22, URM47V4.COMP/TRIG
  N14: Mod1.GPIO25, URM47V3.COMP/TRIG
  N15: Mod1.USB-C, Part4.D+
  N16: J2.pin_1, J3.pin_1, Part6.+, Part7.PWRIN
  GND_3: J3.pin_4, URM47V1.GND, URM47V2.GND, URM47V3.GND, URM47V4.GND
  N17: Part5.+, Part6.-
  N18: Part7.PWM3, J1.pulse

custom parts:
  SparkFun VR IMU Breakout - BNO086 (Qwiic): Virtual reality is in, but you shouldn't have to drop hundreds of dollars to gain access to the technology behind it. Luckily, that's where the SparkFun VR IMU Breakout comes in. At its heart is CEVA’s BNO086, a combination triple-axis accelerometer/gyro/magnetometer System in Package (SiP) with a 32-bit ARM© Cortex™ M0+. The BNO086 Inertial Measurement Unit (IMU) produces accurate rotation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
  Tower Pro SG90 servo: Original file by John De Cristofaro http://www.adafruit.com/products/1449 Adafruit Feedback Servo (Small) Edited by: e-radionica.com 28/9/2015
  Adafruit DRV8871: Crank up your robotics with powerful Adafruit DRV8871 motor driver breakout board. This motor driver has a lot of great specs that make it useful for a wide variety of mechatronics. In particular, the simple resistor-set current limiting and auto-magic PWM support make it super easy to use. Check out the specs for the DRV8871: 6.5V to 45V motor power voltage Up to 5.5V logic level on IN pins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
  ESP32S-HiLetgo: HiLetgo ESP-WROOM-32 ESP32 ESP-32S Development Board 2.4GHz Dual-Mode WiFi + Bluetooth Dual Cores Microcontroller The ESP32 integrated with Antenna switches, RF Balun, power amplifiers, low-noise amplifiers, filters, and management modules, and the entire solution occupies the least area of PCB. 2.4 GHz Wi-Fi plus Bluetooth dual-mode chip, with TSMC Ultra-low power consumption 40nm technology,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
  XL4015 DC-DC CC CV module (blue): XL4015 DC-DC CC/CV module blue
  LIPO-2200mAh: 2200mAh Lipo-battery
  Adafruit PCA9685 PWM/Servo Breakout: Using only two pins, control 16 free-running PWM outputs! I2C-controlled PWM driver with a built in clock. Unlike the TLC5940 family, you do not need to continuously send it signal tying up your microcontroller, its completely free running! 5V compliant, which means you can control it from a 3.3V microcontroller and still safely drive up to 6V outputs (this is good for when you want to control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
  Rechargable Power Bank Battery Pack USB-A (2x Out) USB-C (In/Out): By: Gavin Kress Version: 1 Date: 01/01/2025 Contact: me@gavinkress.org Based off INIU BI-B61 22.5 W | 5V | 4.5A (USB-A)/3A (USB-C)| 37Wh
  Fan - Ventilador: Ventilador de 2 pines, se encuentra comunmente en computadoras de escritorio
